# Fritzing sketch Trilha sonora (saved by Fritzing 0.9.3b)
breadboards: 3

parts:
  Componente1 = Arduino Mega 2560 (Rev3)
  S1 = Pushbutton [package="[SMD]"]
  S2 = Pushbutton [package="[SMD]"]
  S3 = Pushbutton [package="[SMD]"]
  S4 = Pushbutton [package="[SMD]"]
  S5 = Pushbutton [package="[SMD]"]
  S6 = Pushbutton [package="[SMD]"]
  DFPlayer_Mini1 = DFPlayer MINI [package="DIP (Dual Inline) [THT]"]
  R1 = Resistor [tolerance=±5% resistance=220 package="2512 [SMD]"]
  J3 = Basic Servo
  J4 = Basic Servo
  J5 = Basic Servo
  J6 = Basic Servo
  J7 = Basic Servo
  J8 = Basic Servo
  SP1 = SPEAKER [package=pcb_mount_speaker]

nets:
  N1: Componente1.D19/RX1, DFPlayer_Mini1.TX
  N2: Componente1.D18/TX1, R1.Pin_0
  N3: Componente1.D2_PWM, J4.pulse
  N4: Componente1.D3_PWM, J5.pulse
  N5: Componente1.D4_PWM, J6.pulse
  N6: Componente1.D5_PWM, J3.pulse
  N7: Componente1.D6_PWM, J7.pulse
  N8: Componente1.D7_PWM, J8.pulse
  5V: Componente1.5V, DFPlayer_Mini1.VCC
  N9: Componente1.D22, S1.Pin_3, S1.Pin_4
  N10: Componente1.D23, S2.Pin_3, S2.Pin_4
  N11: Componente1.D24, S3.Pin_3, S3.Pin_4
  N12: Componente1.D25, S4.Pin_3, S4.Pin_4
  N13: Componente1.D26, S6.Pin_3, S6.Pin_4
  N14: Componente1.D27, S5.Pin_3, S5.Pin_4
  GND: Componente1.GND, S1.Pin_1, S1.Pin_2, S2.Pin_1, S2.Pin_2, S3.Pin_1, S3.Pin_2, S4.Pin_1, S4.Pin_2, S5.Pin_1, S5.Pin_2, S6.Pin_1, S6.Pin_2, DFPlayer_Mini1.GND
  N15: DFPlayer_Mini1.RX, R1.Pin_1
  N16: DFPlayer_Mini1.SPK1, SP1.-
  N17: DFPlayer_Mini1.SPK2, SP1.+
  GND_2: J3.gnd, J4.gnd, J5.gnd, J6.gnd, J7.gnd, J8.gnd
  VCC: J3.vcc, J4.vcc, J5.vcc, J6.vcc, J7.vcc, J8.vcc

custom parts:
  DFPlayer MINI: MP3 module by DFRobot.com for playing Music from an SD-Card. Supports WAV and MP3 files.
